// Logisim project mapa2.circ as structural Verilog: 2 circuits, main circuit main
module main (
);

  wire keyboard_1_avail, undriven, undriven_2;
  wire [6:0] keyboard_1_data;

  Keyboard #(.buflen(4)) keyboard_1 (
    .re(undriven), .clr(undriven_2), .avail(keyboard_1_avail), .data(keyboard_1_data));  // open: clk
  LogicaEstados LogicaEstados (.in_1(undriven), .in_2(undriven_2), .in_3(keyboard_1_avail), .in_4(keyboard_1_data[0]));
  // Pins of 1 and 7 bits meet at keyboard_1_data
endmodule

module LogicaEstados (
  input  in_1,
  input  in_2,
  input  in_3,
  input  in_4
);

  wire A_q, A_qn, B_q, B_qn, BC_out, BD_out, C_q, C_qn, CD_out, clock_1_out, minus_A_B_out, minus_AB_out,
       minus_AC_out, minus_BD_out;

  Clock clock_1 (.out(clock_1_out));
  J_K_Flip_Flop A (.J(in_1), .clk(clock_1_out), .K(in_1), .Q(A_q), .Qn(A_qn));  // open: preset, en, reset
  J_K_Flip_Flop B (.J(in_2), .clk(clock_1_out), .K(in_2), .Q(B_q), .Qn(B_qn));  // open: preset, en, reset
  J_K_Flip_Flop C (.J(in_3), .clk(clock_1_out), .K(in_3), .Q(C_q), .Qn(C_qn));  // open: preset, en, reset
  J_K_Flip_Flop D (.J(in_4), .clk(clock_1_out), .K(in_4), .Q(in_2));  // open: Qn, preset, en, reset
  and BC (BC_out, B_q, C_q);
  and BCD (in_1, B_q, C_q, in_2);
  and BD (BD_out, B_q, in_2);
  and AD (in_3, A_q, in_2);
  and CD (CD_out, C_q, in_2);
  and minus_AC (minus_AC_out, A_qn, C_q);
  and minus_AB (minus_AB_out, A_qn, B_q);
  and minus_BD (minus_BD_out, B_qn, in_2);
  and minus_A_B (minus_A_B_out, A_qn, B_qn);
  or BD_BC (in_1, BC_out, BD_out);
  or minus_AC_CD (in_2, CD_out, minus_AC_out);
  or minus_AB__BD (in_3, minus_AB_out, minus_BD_out);
  or minus_A_B_C_A (in_4, minus_A_B_out, C_q, A_q);
  or minus_A_B__C_A (in_4, minus_A_B_out, C_qn, A_q);
endmodule
